# Fritzing sketch arduino_rador (saved by Fritzing 0.9.3b)
breadboards: 1

parts:
  Part1 = Arduino Uno (Rev3)
  hc-sr1 = hc-sr04
  M1 = Dagu DGServo 9g (Pan and tilt) [part_number=RS001B]
  J1 = Piezo Speaker

nets:
  N1: Part1.D9_PWM, M1.pulse
  GND: Part1.GND, hc-sr1.GND, M1.gnd, J1.pin1
  N2: Part1.D2, hc-sr1.Echo
  N3: Part1.D3_PWM, hc-sr1.Trig
  N4: Part1.D4, J1.pin2
  VCC: Part1.5V, hc-sr1.VCC, M1.vcc

notes:
  Trigger On D3
  Echo On D2
  servo pin D9
  Buzzer Toggle D4

// code stored in the sketch: Aurdino RAdar.fzz.ino
// Includes the Servo library
#include <Servo.h>. 
// Defines Tirg and Echo pins of the Ultrasonic Sensor
const int trigPin = 3;//orange
const int echoPin = 2;//red white - vcc grey -gnd
// Variables for the duration and the distance
long duration;
int distance;
Servo myServo; // Creates a servo object for controlling the servo motor
void setup() {
  pinMode(trigPin, OUTPUT); // Sets the trigPin as an Output
  pinMode(echoPin, INPUT); // Sets the echoPin as an Input
  pinMode(4,OUTPUT);//yellow
  pinMode(11,OUTPUT);
  Serial.begin(9600);
  myServo.attach(9); // Defines on which pin is the servo motor attached on 9 purple
}
void loop() {
  // rotates the servo motor from 15 to 165 degrees
  for(int i=0;i<=180;i++){  
  myServo.write(i);
  delay(30);
  distance = calculateDistance();// Calls a function for calculating the distance measured by the Ultrasonic sensor for each degree
  
  Serial.print(i); // Sends the current degree into the Serial Port
  Serial.print(","); // Sends addition character right next to the previous value needed later in the Processing IDE for indexing
  Serial.print(distance); // Sends the distance value into the Serial Port
  Serial.print("."); // Sends addition character right next to the previous value needed later in the Processing IDE for indexing
  }
  // Repeats the previous lines from 165 to 15 degrees
  for(int i=180;i>0;i--){  
  myServo.write(i);
  delay(30);
  distance = calculateDistance();
  Serial.print(i);
  Serial.print(",");
  Serial.print(distance);
  Serial.print(".");
  }
}
// Function for calculating the distance measured by the Ultrasonic sensor
int calculateDistance(){ 
  
  digitalWrite(trigPin, LOW); 
  delayMicroseconds(2);
  // Sets the trigPin on HIGH state for 10 micro seconds
  digitalWrite(trigPin, HIGH); 
  delayMicroseconds(10);
  digitalWrite(trigPin, LOW);
  duration = pulseIn(echoPin, HIGH); // Reads the echoPin, returns the sound wave travel time in microseconds
  distance= duration*0.034/2;
  if (distance < 40)
    {
      digitalWrite(4,HIGH);
        digitalWrite(11,HIGH);
      
    }
    else
    {
      digitalWrite(4,LOW);
        digitalWrite(11,LOW);
    }
     return distance;
  
 
}
